# Fritzing sketch PiSofa V1 (saved by Fritzing 0.8.3b)
circuit board: 14.35cm x 5.07cm
breadboards: 1

parts:
  OP-S2 = IC, DIP package, 8 pins [chip_label=IC]
  OP-S3 = IC, DIP package, 8 pins [chip_label=IC]
  T-SW1 = screw terminal, 4 pins
  S3R2 = Resistor [tolerance=±5% resistance=3.3k package=THT]
  S3R1 = Resistor [tolerance=±5% resistance=3.3k package=THT]
  S2R1 = Resistor [tolerance=±5% resistance=3.3k package=THT]
  S2R2 = Resistor [tolerance=±5% resistance=3.3k package=THT]
  S1R2 = Resistor [tolerance=±5% resistance=3.3k package=THT]
  T-S2 = screw terminal, 4 pins
  H-PI = female pin header, 8 pins [form="♀ (female)"]
  T-S1 = screw terminal, 4 pins
  T-S3 = screw terminal, 4 pins
  S1R1 = Resistor [tolerance=±5% resistance=3.3k package=THT]
  S1R3 = Resistor [tolerance=±5% resistance=10k package=THT]
  S3R4 = Resistor [tolerance=±5% resistance=10k package=THT]
  S1R4 = Resistor [tolerance=±5% resistance=10k package=THT]
  S2R3 = Resistor [tolerance=±5% resistance=10k package=THT]
  S2R4 = Resistor [tolerance=±5% resistance=10k package=THT]
  S3R3 = Resistor [tolerance=±5% resistance=10k package=THT]
  DIN-SS3 = DIN-5 jack (MIDI) [package=THT]
  DIN-SS2 = DIN-5 jack (MIDI) [package=THT]
  DIN-SS1 = DIN-5 jack (MIDI) [package=THT]
  DIN-SM1 = DIN-5 jack (MIDI) [package=THT]
  DIN-SM2 = DIN-5 jack (MIDI) [package=THT]
  DIN-SM3 = DIN-5 jack (MIDI) [package=THT]
  OP-S1 = IC, DIP package, 8 pins [chip_label=IC]

nets:
  N1: OP-S2.pin1, S2R1.Pin_1
  GND: OP-S2.pin2, OP-S2.pin4, T-S2.pin4, DIN-SS2.GND, DIN-SM2.GND
  N2: OP-S2.pin3, S2R2.Pin_1
  N3: OP-S2.pin5, OP-S2.pin7, OP-S3.pin5, OP-S3.pin7, H-PI.pin8, OP-S1.pin5, OP-S1.pin7
  N4: OP-S2.pin6, H-PI.pin3, S2R4.Pin_0
  N5: OP-S2.pin8, H-PI.pin4, S2R3.Pin_0
  N6: OP-S3.pin1, S3R1.Pin_1
  GND_2: OP-S3.pin2, OP-S3.pin4, T-S3.pin4, DIN-SS3.GND, DIN-SM3.GND
  N7: OP-S3.pin3, S3R2.Pin_1
  N8: OP-S3.pin6, H-PI.pin1, S3R4.Pin_0
  N9: OP-S3.pin8, H-PI.pin2, S3R3.Pin_0
  N10: T-SW1.pin1, DIN-SS1.3
  N11: T-SW1.pin2, DIN-SS2.3
  N12: T-SW1.pin3, DIN-SS3.3
  N13: S3R2.Pin_0, DIN-SS3.2
  N14: S3R1.Pin_0, DIN-SS3.5
  N15: S2R1.Pin_0, DIN-SS2.5
  N16: S2R2.Pin_0, DIN-SS2.2
  N17: S1R2.Pin_0, DIN-SS1.2
  N18: S1R2.Pin_1, OP-S1.pin3
  N19: T-S2.pin1, DIN-SM2.5
  N20: T-S2.pin2, DIN-SM2.3
  N21: T-S2.pin3, DIN-SM2.2
  N22: H-PI.pin5, S1R4.Pin_0, OP-S1.pin6
  N23: H-PI.pin6, S1R3.Pin_0, OP-S1.pin8
  N24: H-PI.pin7, S1R3.Pin_1, S3R4.Pin_1, S1R4.Pin_1, S2R3.Pin_1, S2R4.Pin_1, S3R3.Pin_1
  N25: T-S1.pin1, DIN-SM1.5
  N26: T-S1.pin2, DIN-SM1.3
  N27: T-S1.pin3, DIN-SM1.2
  GND_3: T-S1.pin4, DIN-SS1.GND, DIN-SM1.GND, OP-S1.pin2, OP-S1.pin4
  N28: T-S3.pin1, DIN-SM3.5
  N29: T-S3.pin2, DIN-SM3.3
  N30: T-S3.pin3, DIN-SM3.2
  N31: S1R1.Pin_0, DIN-SS1.5
  N32: S1R1.Pin_1, OP-S1.pin1

notes:
  PiSofa Version 1.0

custom parts:
  DIN-5 jack (MIDI): Female DIN connector with 5 pins, as used for MIDI and SYNC
