# Fritzing sketch PiSofa V2 - Improved (saved by Fritzing 0.9.0b)
circuit board: 8.73cm x 5.73cm
breadboards: 1

parts:
  Q6 = NPN-Transistor [package="TO92 [THT]"]
  QR6 = Resistor [tolerance=±5% resistance=220 package=THT]
  Q5 = NPN-Transistor [package="TO92 [THT]"]
  QR5 = Resistor [tolerance=±5% resistance=220 package=THT]
  Q3 = NPN-Transistor [package="TO92 [THT]"]
  QR4 = Resistor [tolerance=±5% resistance=220 package=THT]
  QR3 = Resistor [tolerance=±5% resistance=220 package=THT]
  Q2 = NPN-Transistor [package="TO92 [THT]"]
  Q1 = NPN-Transistor [package="TO92 [THT]"]
  QR2 = Resistor [tolerance=±5% resistance=220 package=THT]
  QR1 = Resistor [tolerance=±5% resistance=220 package=THT]
  Q7 = NPN-Transistor [package="TO92 [THT]"]
  QR7 = Resistor [tolerance=±5% resistance=220 package=THT]
  PiHeader = double row female pin header, 26 pins [form="♀ (female)"]
  Q4 = NPN-Transistor [package="TO92 [THT]"]
  OC1 = IC, DIP package, 8 pins [chip_label=IC]
  3_3K = Resistor [tolerance=±5% resistance=220 package=THT]
  3_3K_2 = Resistor [tolerance=±5% resistance=220 package=THT]
  3_3K_3 = Resistor [tolerance=±5% resistance=220 package=THT]
  3_3K_4 = Resistor [tolerance=±5% resistance=220 package=THT]
  OC2 = IC, DIP package, 8 pins [chip_label=IC]
  3_3K_5 = Resistor [tolerance=±5% resistance=220 package=THT]
  3_3K_6 = Resistor [tolerance=±5% resistance=220 package=THT]
  OC3 = IC, DIP package, 8 pins [chip_label=IC]
  10K = Resistor [tolerance=±5% resistance=220 package=THT]
  10K_2 = Resistor [tolerance=±5% resistance=220 package=THT]
  10K_3 = Resistor [tolerance=±5% resistance=220 package=THT]
  10K_4 = Resistor [tolerance=±5% resistance=220 package=THT]
  10K_5 = Resistor [tolerance=±5% resistance=220 package=THT]
  10K_6 = Resistor [tolerance=±5% resistance=220 package=THT]
  SS3 = Screw terminal - 4 pins [package=THT]
  SM2 = Screw terminal - 4 pins [package=THT]
  SM3 = Screw terminal - 4 pins [package=THT]
  SS1 = Screw terminal - 4 pins [package=THT]
  SS2 = Screw terminal - 4 pins [package=THT]
  SM1 = Screw terminal - 4 pins [package=THT]
  RELAY4 = RELAY-SOLIDSTATE [package=relay-s108t02]
  RELAY1 = RELAY-SOLIDSTATE [package=relay-s108t02]
  RELAY3 = RELAY-SOLIDSTATE [package=relay-s108t02]
  RELAY7 = RELAY-SOLIDSTATE [package=relay-s108t02]
  RELAY5 = RELAY-SOLIDSTATE [package=relay-s108t02]
  RELAY2 = RELAY-SOLIDSTATE [package=relay-s108t02]
  RELAY6 = RELAY-SOLIDSTATE [package=relay-s108t02]
  D7 = Diode [package=diode-1n4001]
  D5 = Diode [package=diode-1n4001]
  D2 = Diode [package=diode-1n4001]
  D6 = Diode [package=diode-1n4001]
  D3 = Diode [package=diode-1n4001]
  D4 = Diode [package=diode-1n4001]
  D1 = Diode [package=diode-1n4001]

nets:
  N1: Q6.E, Q5.E, Q3.E, Q2.E, Q1.E, Q7.E, PiHeader.pin13, Q4.E
  N2: Q6.B, QR6.Pin_1
  N3: Q6.C, RELAY6.+, D6.A
  N4: QR6.Pin_0, PiHeader.pin11
  N5: Q5.B, QR5.Pin_1
  N6: Q5.C, RELAY5.+, D5.A
  N7: QR5.Pin_0, PiHeader.pin10
  N8: Q3.B, QR3.Pin_1
  N9: Q3.C, RELAY3.+, D3.A
  N10: QR4.Pin_0, PiHeader.pin8
  N11: QR4.Pin_1, Q4.B
  N12: QR3.Pin_0, PiHeader.pin15
  N13: Q2.B, QR2.Pin_1
  N14: Q2.C, RELAY2.+, D2.A
  N15: Q1.B, QR1.Pin_1
  N16: Q1.C, RELAY1.+, D1.A
  N17: QR2.Pin_0, PiHeader.pin14
  N18: QR1.Pin_0, PiHeader.pin12
  N19: Q7.B, QR7.Pin_0
  N20: Q7.C, RELAY7.+, D7.A
  N21: QR7.Pin_1, PiHeader.pin7
  N22: PiHeader.pin2, OC2.pin6, 10K_4.Pin_0
  N23: PiHeader.pin3, OC2.pin8, 10K_3.Pin_0
  N24: PiHeader.pin4, OC3.pin6, 10K_6.Pin_0
  N25: PiHeader.pin5, OC1.pin5, OC1.pin7, OC2.pin5, OC2.pin7, OC3.pin5, OC3.pin7
  N26: PiHeader.pin6, OC3.pin8, 10K_5.Pin_0
  N27: PiHeader.pin9, 10K.Pin_1, 10K_2.Pin_1, 10K_3.Pin_1, 10K_4.Pin_1, 10K_5.Pin_1, 10K_6.Pin_1
  N28: PiHeader.pin19, OC1.pin6, 10K.Pin_0
  N29: PiHeader.pin21, OC1.pin8, 10K_2.Pin_0
  N30: PiHeader.pin26, RELAY4.-, RELAY1.-, RELAY3.-, RELAY7.-, RELAY5.-, RELAY2.-, RELAY6.-, D7.C, D5.C, D2.C, D6.C, D3.C, D4.C, D1.C
  N31: Q4.C, RELAY4.+, D4.A
  N32: OC1.pin1, 3_3K.Pin_0
  N33: OC1.pin2, OC1.pin4, OC2.pin2, OC2.pin4, OC3.pin2, OC3.pin4, SS3.pin4, SM3.pin4, SS1.pin4, SS2.pin4, RELAY7.NO, RELAY5.NO, RELAY6.NO
  N34: OC1.pin3, 3_3K_2.Pin_0
  N35: 3_3K.Pin_1, SS3.pin1
  N36: 3_3K_2.Pin_1, SS3.pin3
  N37: 3_3K_3.Pin_0, OC2.pin1
  N38: 3_3K_3.Pin_1, SS2.pin1
  N39: 3_3K_4.Pin_0, OC2.pin3
  N40: 3_3K_4.Pin_1, SS2.pin3
  N41: 3_3K_5.Pin_0, OC3.pin3
  N42: 3_3K_5.Pin_1, SS1.pin3
  N43: 3_3K_6.Pin_0, OC3.pin1
  N44: 3_3K_6.Pin_1, SS1.pin1
  N45: SS3.pin2, SS1.pin2, SS2.pin2, RELAY7.C
  N46: SM2.pin1, RELAY4.C
  N47: SM2.pin2, RELAY4.NC, RELAY3.NC
  N48: SM2.pin3, RELAY3.C
  N49: SM2.pin4, RELAY4.NO, RELAY3.NO
  N50: SM3.pin1, RELAY6.C
  N51: SM3.pin2, RELAY7.NC, RELAY5.NC, RELAY6.NC
  N52: SM3.pin3, RELAY5.C
  N53: SM1.pin1, RELAY2.C
  N54: SM1.pin2, RELAY1.NC, RELAY2.NC
  N55: SM1.pin3, RELAY1.C
  N56: SM1.pin4, RELAY1.NO, RELAY2.NO

notes:
  PiSofa V2.0

custom parts:
  Screw terminal - 4 pins: Screw terminal with 4 pins
  RELAY-SOLIDSTATE: SPST SS relay
