# Fritzing sketch PiSofa V2 - Untested (saved by Fritzing 0.8.5b)
circuit board: 8.73cm x 5.73cm
breadboards: 1

parts:
  Q6 = NPN-Transistor [package="TO92 [THT]"]
  2_2K = Resistor [tolerance=±5% resistance=220 package=THT]
  Q5 = NPN-Transistor [package="TO92 [THT]"]
  2_2K_2 = Resistor [tolerance=±5% resistance=220 package=THT]
  Q3 = NPN-Transistor [package="TO92 [THT]"]
  2_2K_3 = Resistor [tolerance=±5% resistance=220 package=THT]
  2_2K_4 = Resistor [tolerance=±5% resistance=220 package=THT]
  Q2 = NPN-Transistor [package="TO92 [THT]"]
  Q1 = NPN-Transistor [package="TO92 [THT]"]
  2_2K_5 = Resistor [tolerance=±5% resistance=220 package=THT]
  2_2K_6 = Resistor [tolerance=±5% resistance=220 package=THT]
  Q7 = NPN-Transistor [package="TO92 [THT]"]
  2_2K_7 = Resistor [tolerance=±5% resistance=220 package=THT]
  RELAY7 = RELAY-SOLIDSTATE [package=relay-s108t02]
  RELAY6 = RELAY-SOLIDSTATE [package=relay-s108t02]
  RELAY3 = RELAY-SOLIDSTATE [package=relay-s108t02]
  RELAY4 = RELAY-SOLIDSTATE [package=relay-s108t02]
  RELAY1 = RELAY-SOLIDSTATE [package=relay-s108t02]
  D6 = Diode [package=diode-1n4001]
  D5 = Diode [package=diode-1n4001]
  D4 = Diode [package=diode-1n4001]
  D3 = Diode [package=diode-1n4001]
  D2 = Diode [package=diode-1n4001]
  D1 = Diode [package=diode-1n4001]
  PiHeader = double row female pin header, 26 pins [form="♀ (female)"]
  D8 = Diode [package=diode-1n4001]
  RELAY5 = RELAY-SOLIDSTATE [package=relay-s108t02]
  RELAY2 = RELAY-SOLIDSTATE [package=relay-s108t02]
  Q4 = NPN-Transistor [package="TO92 [THT]"]
  OC1 = IC, DIP package, 8 pins [chip_label=IC]
  3_3K = Resistor [tolerance=±5% resistance=220 package=THT]
  3_3K_2 = Resistor [tolerance=±5% resistance=220 package=THT]
  3_3K_3 = Resistor [tolerance=±5% resistance=220 package=THT]
  3_3K_4 = Resistor [tolerance=±5% resistance=220 package=THT]
  OC2 = IC, DIP package, 8 pins [chip_label=IC]
  3_3K_5 = Resistor [tolerance=±5% resistance=220 package=THT]
  3_3K_6 = Resistor [tolerance=±5% resistance=220 package=THT]
  OC3 = IC, DIP package, 8 pins [chip_label=IC]
  D7 = Diode [package=diode-1n4001]
  10K = Resistor [tolerance=±5% resistance=220 package=THT]
  10K_2 = Resistor [tolerance=±5% resistance=220 package=THT]
  10K_3 = Resistor [tolerance=±5% resistance=220 package=THT]
  10K_4 = Resistor [tolerance=±5% resistance=220 package=THT]
  10K_5 = Resistor [tolerance=±5% resistance=220 package=THT]
  10K_6 = Resistor [tolerance=±5% resistance=220 package=THT]
  SS3 = Screw terminal - 4 pins [package=THT]
  SM2 = Screw terminal - 4 pins [package=THT]
  SM3 = Screw terminal - 4 pins [package=THT]
  SS1 = Screw terminal - 4 pins [package=THT]
  SS2 = Screw terminal - 4 pins [package=THT]
  SM1 = Header4

nets:
  N1: Q6.E, Q5.E, Q3.E, Q2.E, Q1.E, Q7.E, PiHeader.pin13, Q4.E, 10K.Pin_1, 10K_2.Pin_1, 10K_3.Pin_1, 10K_4.Pin_1, 10K_5.Pin_1, 10K_6.Pin_1
  N2: Q6.B, 2_2K.Pin_1
  N3: Q6.C, RELAY6.+, D6.A
  N4: 2_2K.Pin_0, PiHeader.pin8
  N5: Q5.B, 2_2K_2.Pin_1
  N6: Q5.C, D5.A, RELAY5.+
  N7: 2_2K_2.Pin_0, PiHeader.pin10
  N8: Q3.B, 2_2K_4.Pin_1
  N9: Q3.C, RELAY3.+, D3.A
  N10: 2_2K_3.Pin_0, PiHeader.pin11
  N11: 2_2K_3.Pin_1, Q4.B
  N12: 2_2K_4.Pin_0, PiHeader.pin15
  N13: Q2.B, 2_2K_5.Pin_1
  N14: Q2.C, D2.A, RELAY2.+
  N15: Q1.B, 2_2K_6.Pin_1
  N16: Q1.C, RELAY1.+, D1.A
  N17: 2_2K_5.Pin_0, PiHeader.pin14
  N18: 2_2K_6.Pin_0, PiHeader.pin12
  N19: Q7.B, 2_2K_7.Pin_0
  N20: Q7.C, RELAY7.+, D7.A
  N21: 2_2K_7.Pin_1, PiHeader.pin7
  N22: RELAY7.-, RELAY6.-, RELAY3.-, RELAY4.-, RELAY1.-, D6.C, D5.C, D4.C, D3.C, D2.C, D1.C, D8.C, RELAY5.-, RELAY2.-, D7.C
  N23: RELAY7.C, SS3.pin2, SS1.pin2, SS2.pin2
  N24: RELAY7.NO, RELAY6.NO, RELAY5.NO, OC1.pin2, OC1.pin4, OC2.pin2, OC2.pin4, OC3.pin2, OC3.pin4, SS3.pin4, SM3.pin4, SS1.pin4, SS2.pin4
  N25: RELAY7.NC, RELAY6.NC, RELAY5.NC, SM3.pin2
  N26: RELAY6.C, SM3.pin1
  N27: RELAY3.C, SM2.pin3
  N28: RELAY3.NO, RELAY4.NO, SM2.pin4
  N29: RELAY3.NC, RELAY4.NC, SM2.pin2
  N30: RELAY4.+, D4.A, Q4.C
  N31: RELAY4.C, SM2.pin1
  N32: RELAY1.C, SM1.connector2
  N33: RELAY1.NO, RELAY2.NO, SM1.connector3
  N34: RELAY1.NC, RELAY2.NC, SM1.connector1
  N35: PiHeader.pin2, OC2.pin6, 10K_4.Pin_0
  N36: PiHeader.pin3, OC2.pin8, 10K_3.Pin_0
  N37: PiHeader.pin4, OC3.pin6, 10K_6.Pin_0
  N38: PiHeader.pin6, OC3.pin8, 10K_5.Pin_0
  N39: PiHeader.pin9, OC1.pin5, OC1.pin7, OC2.pin5, OC2.pin7, OC3.pin5, OC3.pin7
  N40: PiHeader.pin19, OC1.pin6, 10K.Pin_0
  N41: PiHeader.pin21, OC1.pin8, 10K_2.Pin_0
  N42: PiHeader.pin26, D8.A
  N43: RELAY5.C, SM3.pin3
  N44: RELAY2.C, SM1.connector0
  N45: OC1.pin1, 3_3K.Pin_0
  N46: OC1.pin3, 3_3K_2.Pin_0
  N47: 3_3K.Pin_1, SS3.pin1
  N48: 3_3K_2.Pin_1, SS3.pin3
  N49: 3_3K_3.Pin_0, OC2.pin1
  N50: 3_3K_3.Pin_1, SS2.pin1
  N51: 3_3K_4.Pin_0, OC2.pin3
  N52: 3_3K_4.Pin_1, SS2.pin3
  N53: 3_3K_5.Pin_0, OC3.pin3
  N54: 3_3K_5.Pin_1, SS1.pin3
  N55: 3_3K_6.Pin_0, OC3.pin1
  N56: 3_3K_6.Pin_1, SS1.pin1

notes:
  PiSofa V2.0

custom parts:
  RELAY-SOLIDSTATE: SPST SS relay
  Screw terminal - 4 pins: Screw terminal with 4 pins
