# Fritzing sketch PiSofa V2+ - save serial (saved by Fritzing 0.9.0b)
circuit board: 8.5cm x 5.6cm
breadboards: 1

parts:
  Q6 = NPN-Transistor [package="TO92 [THT]"]
  QR6 = Resistor [tolerance=±5% resistance=220 package=THT]
  Q5 = NPN-Transistor [package="TO92 [THT]"]
  QR5 = Resistor [tolerance=±5% resistance=220 package=THT]
  QR4 = Resistor [tolerance=±5% resistance=220 package=THT]
  QR3 = Resistor [tolerance=±5% resistance=220 package=THT]
  Q2 = NPN-Transistor [package="TO92 [THT]"]
  Q1 = NPN-Transistor [package="TO92 [THT]"]
  QR2 = Resistor [tolerance=±5% resistance=220 package=THT]
  QR1 = Resistor [tolerance=±5% resistance=220 package=THT]
  Q7 = NPN-Transistor [package="TO92 [THT]"]
  QR7 = Resistor [tolerance=±5% resistance=220 package=THT]
  Q4 = NPN-Transistor [package="TO92 [THT]"]
  OC1 = IC, DIP package, 8 pins [chip_label=IC]
  3_3K = Resistor [tolerance=±5% resistance=220 package=THT]
  3_3K_2 = Resistor [tolerance=±5% resistance=220 package=THT]
  3_3K_3 = Resistor [tolerance=±5% resistance=220 package=THT]
  3_3K_4 = Resistor [tolerance=±5% resistance=220 package=THT]
  OC2 = IC, DIP package, 8 pins [chip_label=IC]
  3_3K_5 = Resistor [tolerance=±5% resistance=220 package=THT]
  3_3K_6 = Resistor [tolerance=±5% resistance=220 package=THT]
  OC3 = IC, DIP package, 8 pins [chip_label=IC]
  10K = Resistor [tolerance=±5% resistance=220 package=THT]
  10K_2 = Resistor [tolerance=±5% resistance=220 package=THT]
  10K_3 = Resistor [tolerance=±5% resistance=220 package=THT]
  10K_4 = Resistor [tolerance=±5% resistance=220 package=THT]
  10K_5 = Resistor [tolerance=±5% resistance=220 package=THT]
  SM2 = Screw terminal - 4 pins [package=THT]
  SM3 = Screw terminal - 4 pins [package=THT]
  SS1 = Screw terminal - 4 pins [package=THT]
  SS2 = Screw terminal - 4 pins [package=THT]
  SM1 = Screw terminal - 4 pins [package=THT]
  RELAY4 = RELAY-SOLIDSTATE [package=relay-s108t02]
  RELAY1 = RELAY-SOLIDSTATE [package=relay-s108t02]
  RELAY3 = RELAY-SOLIDSTATE [package=relay-s108t02]
  RELAY7 = RELAY-SOLIDSTATE [package=relay-s108t02]
  RELAY5 = RELAY-SOLIDSTATE [package=relay-s108t02]
  RELAY2 = RELAY-SOLIDSTATE [package=relay-s108t02]
  RELAY6 = RELAY-SOLIDSTATE [package=relay-s108t02]
  PiHeader = double row female pin header, 40 pins [form="♀ (female)"]
  D6 = Diode [package=diode-1n4001]
  D4 = Diode [package=diode-1n4001]
  D1 = Diode [package=diode-1n4001]
  D5 = Diode [package=diode-1n4001]
  D7 = Diode [package=diode-1n4001]
  D2 = Diode [package=diode-1n4001]
  D3 = Diode [package=diode-1n4001]
  Q3 = NPN-Transistor [package="TO92 [THT]"]
  SS3 = Screw terminal - 4 pins [package=THT]
  10K_6 = Resistor [tolerance=±5% resistance=220 package=THT]

nets:
  N1: Q6.E, Q5.E, Q2.E, Q1.E, Q7.E, Q4.E, PiHeader.pin13, Q3.E
  N2: Q6.B, QR6.Pin_1
  N3: Q6.C, RELAY6.+, D6.A
  N4: QR6.Pin_0, PiHeader.pin16
  N5: Q5.B, QR5.Pin_1
  N6: Q5.C, RELAY5.+, D5.A
  N7: QR5.Pin_0, PiHeader.pin17
  N8: QR4.Pin_0, Q4.B
  N9: QR4.Pin_1, PiHeader.pin18
  N10: QR3.Pin_0, Q3.B
  N11: QR3.Pin_1, PiHeader.pin19
  N12: Q2.B, QR2.Pin_0
  N13: Q2.C, RELAY2.+, D2.A
  N14: Q1.B, QR1.Pin_0
  N15: Q1.C, RELAY1.+, D1.A
  N16: QR2.Pin_1, PiHeader.pin22
  N17: QR1.Pin_1, PiHeader.pin21
  N18: Q7.B, QR7.Pin_0
  N19: Q7.C, RELAY7.+, D7.A
  N20: QR7.Pin_1, PiHeader.pin15
  N21: Q4.C, RELAY4.+, D4.A
  N22: OC1.pin1, 3_3K.Pin_0
  N23: OC1.pin2, OC1.pin4, OC2.pin2, OC2.pin4, OC3.pin2, OC3.pin4, SM3.pin4, SS1.pin4, SS2.pin4, RELAY7.NO, RELAY5.NO, RELAY6.NO, SS3.pin4
  N24: OC1.pin3, 3_3K_2.Pin_0
  N25: OC1.pin5, OC1.pin7, OC2.pin5, OC2.pin7, OC3.pin5, OC3.pin7, PiHeader.pin5
  N26: OC1.pin6, 10K.Pin_0, PiHeader.pin33
  N27: OC1.pin8, PiHeader.pin35, 10K_6.Pin_0
  N28: 3_3K.Pin_1, SS3.pin1
  N29: 3_3K_2.Pin_1, SS3.pin3
  N30: 3_3K_3.Pin_0, OC2.pin1
  N31: 3_3K_3.Pin_1, SS2.pin1
  N32: 3_3K_4.Pin_0, OC2.pin3
  N33: 3_3K_4.Pin_1, SS2.pin3
  N34: OC2.pin6, 10K_3.Pin_0, PiHeader.pin4
  N35: OC2.pin8, 10K_2.Pin_0, PiHeader.pin6
  N36: 3_3K_5.Pin_0, OC3.pin3
  N37: 3_3K_5.Pin_1, SS1.pin3
  N38: 3_3K_6.Pin_0, OC3.pin1
  N39: 3_3K_6.Pin_1, SS1.pin1
  N40: OC3.pin6, 10K_5.Pin_0, PiHeader.pin7
  N41: OC3.pin8, 10K_4.Pin_0, PiHeader.pin8
  N42: 10K.Pin_1, 10K_2.Pin_1, 10K_3.Pin_1, 10K_4.Pin_1, 10K_5.Pin_1, PiHeader.pin9, 10K_6.Pin_1
  N43: SM2.pin1, RELAY4.C
  N44: SM2.pin2, RELAY4.NC, RELAY3.NC
  N45: SM2.pin3, RELAY3.C
  N46: SM2.pin4, RELAY4.NO, RELAY3.NO
  N47: SM3.pin1, RELAY6.C
  N48: SM3.pin2, RELAY7.NC, RELAY5.NC, RELAY6.NC
  N49: SM3.pin3, RELAY5.C
  N50: SS1.pin2, SS2.pin2, RELAY7.C, SS3.pin2
  N51: SM1.pin1, RELAY2.C
  N52: SM1.pin2, RELAY1.NC, RELAY2.NC
  N53: SM1.pin3, RELAY1.C
  N54: SM1.pin4, RELAY1.NO, RELAY2.NO
  N55: RELAY4.-, RELAY1.-, RELAY3.-, RELAY7.-, RELAY5.-, RELAY2.-, RELAY6.-, PiHeader.pin40, D6.C, D4.C, D1.C, D5.C, D7.C, D2.C, D3.C
  N56: RELAY3.+, D3.A, Q3.C

notes:
  PiSofa V2+

custom parts:
  Screw terminal - 4 pins: Screw terminal with 4 pins
  RELAY-SOLIDSTATE: SPST SS relay
