# Fritzing sketch PiSofa V2++ (saved by Fritzing 0.9.0b)
circuit board: 8.54428cm x 5.64269cm
breadboards: 1

parts:
  Q6 = NPN-Transistor [package="TO92 [THT]"]
  QR6 = Resistor [tolerance=±5% resistance=220 package=THT]
  Q5 = NPN-Transistor [package="TO92 [THT]"]
  QR5 = Resistor [tolerance=±5% resistance=220 package=THT]
  QR4 = Resistor [tolerance=±5% resistance=220 package=THT]
  QR3 = Resistor [tolerance=±5% resistance=220 package=THT]
  Q2 = NPN-Transistor [package="TO92 [THT]"]  # not connected
  Q1 = NPN-Transistor [package="TO92 [THT]"]
  QR2 = Resistor [tolerance=±5% resistance=220 package=THT]
  QR1 = Resistor [tolerance=±5% resistance=220 package=THT]
  Q7 = NPN-Transistor [package="TO92 [THT]"]
  QR7 = Resistor [tolerance=±5% resistance=220 package=THT]  # not connected
  Q4 = NPN-Transistor [package="TO92 [THT]"]
  OC1 = IC, DIP package, 8 pins [chip_label=IC]  # not connected
  3_3K = Resistor [tolerance=±5% resistance=220 package=THT]  # not connected
  3_3K_2 = Resistor [tolerance=±5% resistance=220 package=THT]  # not connected
  3_3K_3 = Resistor [tolerance=±5% resistance=220 package=THT]  # not connected
  3_3K_4 = Resistor [tolerance=±5% resistance=220 package=THT]  # not connected
  OC2 = IC, DIP package, 8 pins [chip_label=IC]  # not connected
  3_3K_5 = Resistor [tolerance=±5% resistance=220 package=THT]  # not connected
  3_3K_6 = Resistor [tolerance=±5% resistance=220 package=THT]  # not connected
  OC3 = IC, DIP package, 8 pins [chip_label=IC]  # not connected
  10K = Resistor [tolerance=±5% resistance=220 package=THT]  # not connected
  10K_2 = Resistor [tolerance=±5% resistance=220 package=THT]  # not connected
  10K_3 = Resistor [tolerance=±5% resistance=220 package=THT]  # not connected
  10K_4 = Resistor [tolerance=±5% resistance=220 package=THT]  # not connected
  10K_5 = Resistor [tolerance=±5% resistance=220 package=THT]  # not connected
  10K_6 = Resistor [tolerance=±5% resistance=220 package=THT]  # not connected
  SM2 = Screw terminal - 4 pins [package=THT]
  SM3 = Screw terminal - 4 pins [package=THT]
  SS1 = Screw terminal - 4 pins [package=THT]
  SS2 = Screw terminal - 4 pins [package=THT]
  SM1 = Screw terminal - 4 pins [package=THT]
  RELAY4 = RELAY-SOLIDSTATE [package=relay-s108t02]
  RELAY1 = RELAY-SOLIDSTATE [package=relay-s108t02]
  RELAY3 = RELAY-SOLIDSTATE [package=relay-s108t02]
  RELAY7 = RELAY-SOLIDSTATE [package=relay-s108t02]  # not connected
  RELAY5 = RELAY-SOLIDSTATE [package=relay-s108t02]
  RELAY2 = RELAY-SOLIDSTATE [package=relay-s108t02]
  RELAY6 = RELAY-SOLIDSTATE [package=relay-s108t02]
  PiHeader = double row female pin header, 40 pins [form="♀ (female)"]
  D6 = Diode [package=diode-1n4001]
  D4 = Diode [package=diode-1n4001]
  D1 = Diode [package=diode-1n4001]
  D5 = Diode [package=diode-1n4001]  # not connected
  D7 = Diode [package=diode-1n4001]
  D2 = Diode [package=diode-1n4001]
  D3 = Diode [package=diode-1n4001]
  Q3 = NPN-Transistor [package="TO92 [THT]"]
  SS3 = Screw terminal - 4 pins [package=THT]

nets:
  N1: Q6.E, RELAY3.+
  N2: Q6.B, QR4.Pin_0
  N3: Q6.C, Q5.C, Q1.C, Q7.C, Q4.C, D6.A, D4.A, D1.A, D7.A, D2.A, D3.A, Q3.C
  N4: QR6.Pin_0, Q4.B
  N5: QR6.Pin_1, PiHeader.pin32
  N6: Q5.E, RELAY6.+
  N7: Q5.B, QR1.Pin_0
  N8: QR5.Pin_0, Q3.B
  N9: QR5.Pin_1, PiHeader.pin35
  N10: QR4.Pin_1, PiHeader.pin36
  N11: QR3.Pin_0, Q1.B
  N12: QR3.Pin_1, PiHeader.pin37
  N13: Q1.E, RELAY4.+
  N14: QR2.Pin_0, Q7.B
  N15: QR2.Pin_1, PiHeader.pin38
  N16: QR1.Pin_1, PiHeader.pin39
  N17: Q7.E, RELAY5.+
  N18: Q4.E, RELAY2.+
  N19: SM2.pin1, RELAY3.C
  N20: SM2.pin2, RELAY4.NC, RELAY3.NC
  N21: SM2.pin3, RELAY4.NO, RELAY3.NO
  N22: SM2.pin4, RELAY4.C
  N23: SM3.pin1, RELAY5.C
  N24: SM3.pin2, RELAY5.NC, RELAY6.NC
  N25: SM3.pin3, RELAY5.NO, RELAY6.NO
  N26: SM3.pin4, RELAY6.C
  N27: SS1.pin3, SS2.pin3, SM1.pin2, RELAY1.NC, RELAY2.NC, SS3.pin3
  N28: SS1.pin4, SS2.pin4, SM1.pin3, RELAY1.NO, RELAY2.NO, SS3.pin4
  N29: SM1.pin1, RELAY1.C
  N30: SM1.pin4, RELAY2.C
  N31: RELAY4.-, RELAY1.-, RELAY3.-, RELAY5.-, RELAY2.-, RELAY6.-, PiHeader.pin20, D6.C, D4.C, D1.C, D7.C, D2.C, D3.C
  N32: RELAY1.+, Q3.E

notes:
  PiSofa V2+

custom parts:
  Screw terminal - 4 pins: Screw terminal with 4 pins
  RELAY-SOLIDSTATE: SPST SS relay
